# Fritzing sketch Troca de energia automática (saved by Fritzing 0.9.3b)
breadboards: 1

parts:
  U1 = 2ChannelRelay
  Componente1 = Intel Galileo
  Componente2 = Lilypad Battery Connect
  Componente3 = ACS712 Low Current Sensor Board v12
  LED1 = LEDs [package=led10mm]
  LED2 = smd LED [color="Red (633nm)" package="0805 [SMD]"]
  R1 = Resistor [tolerance=±5% resistance=220 package="0402 [SMD]"]

nets:
  N1: U1.connector0, Componente1.D8
  GND: U1.connector1, Componente1.GND, Componente3.GND, LED2.anode
  N2: U1.connector3, Componente1.D4
  N3: U1.connector7, Componente3.IP+
  N4: U1.connector9, LED1.C
  N5: Componente1.A0, Componente3.VO
  N6: Componente1.D2, R1.Pin_0
  5V: Componente1.5V, Componente3.5V
  N7: Componente2.-, LED1.A
  N8: Componente2.+, Componente3.IP-
  N9: LED2.cathode, R1.Pin_1
